# Fritzing sketch hc-sr04-sensor-circuit-diagram (saved by Fritzing 0.9.4)
breadboards: 1

parts:
  WeMos_D1_Mini1 = WeMos D1 Mini
  R1 = Resistor [tolerance=±5% resistance=330 package=THT]
  R2 = Resistor [tolerance=±5% resistance=330 package=THT]
  HC-SR04_Sensor_1 = HC-SR04 Ultrasonic Distance Sensor

nets:
  5V: WeMos_D1_Mini1.5V, HC-SR04_Sensor_1.VCC
  N1: WeMos_D1_Mini1.D1, R1.Pin_1, R2.Pin_1
  N2: WeMos_D1_Mini1.D2, HC-SR04_Sensor_1.TRIG
  N3: WeMos_D1_Mini1.G, R1.Pin_0, HC-SR04_Sensor_1.ECHO
  N4: R2.Pin_0, HC-SR04_Sensor_1.GND
